# Fritzing sketch sketch (saved by Fritzing 0.9.2b)
breadboards: 1

parts:
  Part1 = Intel Edison Arduinobreakout
  U1 = LIPO-2000mAh [package=lipo-2000]
  CHARGER1 = USB_LiIon_LiPoly_Charger_v1.2
  Solar_pannel1 = solar_pannel
  PIR1 = PIR sensor
  R1 = Resistor [tolerance=±5% resistance=180 package="0402 [SMD]"]
  Q1 = LTR-301 [package=ltr-301]
  IC1 = IC, DIP package, 4 pins [chip_label=IC]

nets:
  N1: Part1.D8, PIR1.SIG
  5V: Part1.5V, PIR1.VDD, Q1.E
  GND: Part1.GND, PIR1.GND, R1.Pin_1, IC1.pin2
  N2: Part1.VIN, IC1.pin1
  N3: U1.+, CHARGER1.batt_plus_1
  N4: U1.-, CHARGER1.batt_minus_1
  N5: CHARGER1.dcin_minus_1, Solar_pannel1.aún_sin_nombre#0
  N6: CHARGER1.dcin_plus_1, Solar_pannel1.aún_sin_nombre#1
  N7: CHARGER1.load_minus_1, IC1.pin3
  N8: CHARGER1.load_plus_1, IC1.pin4
  N9: R1.Pin_0, Q1.C

notes:
  Step Up to 5V
  5V Step Up
  Light for illuminating the bird nest with IR
  Lithium battery

custom parts:
  solar_pannel: Solar pannel
